// Logisim project 1_cameronpierce.circ as structural Verilog: 1 circuit, main circuit main
module main (
  input  in_1,
  input  in_2,
  input  in_3,
  input  in_4,
  input  in_5,
  output out_6,
  output out_7,
  output out_8
);

  wire nand_1_out, nand_2_out, nand_4_out;

  nand nand_1 (nand_1_out, in_1, in_2);
  nand nand_2 (nand_2_out, in_4, in_4);
  not nand_3 (out_8, in_5);  // NAND_Gate
  nand nand_4 (nand_4_out, in_3, in_3);
  nand nand_5 (out_7, nand_4_out, nand_2_out);
  not nand_6 (out_6, nand_1_out);  // NAND_Gate
endmodule
