// Logisim project 3_cameronpierce.circ as structural Verilog: 2 circuits, main circuit singlebit
module singlebit (
  input  CarryIn,
  input  A,
  input  B,
  output Sum,
  output CarryOut
);

  wire and_1_out, and_2_out, xor_1_out;

  xor xor_1 (xor_1_out, A, B);
  and and_1 (and_1_out, A, B);
  and and_2 (and_2_out, CarryIn, xor_1_out);
  xor xor_2 (Sum, xor_1_out, CarryIn);
  or or_1 (CarryOut, and_2_out, and_1_out);
endmodule

module FourBitFullerAdder (
  input  CarryIn,
  input  [3:0] A,
  input  [3:0] B,
  output [3:0] Sum,
  output CarryOut
);

  wire singlebit_1_carryout, singlebit_2_carryout, singlebit_3_carryout;

  singlebit singlebit_1 (.CarryIn(CarryIn), .A(A[0]), .B(B[0]), .Sum(Sum[0]), .CarryOut(singlebit_1_carryout));
  singlebit singlebit_2 (
    .CarryIn(singlebit_1_carryout), .A(A[1]), .B(B[1]), .Sum(Sum[1]), .CarryOut(singlebit_2_carryout));
  singlebit singlebit_3 (
    .CarryIn(singlebit_2_carryout), .A(A[2]), .B(B[2]), .Sum(Sum[2]), .CarryOut(singlebit_3_carryout));
  singlebit singlebit_4 (.CarryIn(singlebit_3_carryout), .A(A[3]), .B(B[3]), .Sum(Sum[3]), .CarryOut(CarryOut));
endmodule
