// Logisim project 4_cameronpierce.circ as structural Verilog: 1 circuit, main circuit main
module main (
  input  in_1,
  input  [1:0] in_2,
  input  in_3,
  input  in_4,
  input  in_5,
  output out_6
);

  wire adder_1_out, and_1_out, multiplexer_1_out, multiplexer_2_out, not_1_out, not_2_out, or_1_out;

  not not_1 (not_1_out, in_3);
  not not_2 (not_2_out, in_4);
  Multiplexer multiplexer_1 (.in0(in_3), .in1(not_1_out), .out(multiplexer_1_out), .sel(in_1));
  Multiplexer multiplexer_2 (.in0(in_4), .in1(not_2_out), .out(multiplexer_2_out), .sel(in_5));
  and and_1 (and_1_out, multiplexer_1_out, multiplexer_2_out);
  or or_1 (or_1_out, multiplexer_1_out, multiplexer_2_out);
  Adder #(.width(1)) adder_1 (.a(multiplexer_1_out), .b(multiplexer_2_out), .out(adder_1_out));  // open: cin, cout
  Multiplexer #(.select(2)) multiplexer_3 (
    .in0(and_1_out), .in1(or_1_out), .in2(adder_1_out), .out(out_6), .sel(in_2));  // open: in3
endmodule
