// Logisim project 5_cameronpierce.circ as structural Verilog: 1 circuit, main circuit main
module main (
  input  in_1,
  input  in_2,
  input  in_3,
  output out_4,
  output out_5,
  output out_6,
  output out_7
);

  wire clock_1_out, nand_1_out, nand_2_out, nand_3_out, nand_4_out, not_1_out, not_2_out;

  not not_1 (not_1_out, in_1);
  Clock clock_1 (.out(clock_1_out));
  not not_2 (not_2_out, in_3);
  nand nand_1 (nand_1_out, in_1, in_1);
  nand nand_2 (nand_2_out, in_1, not_1_out);
  nand nand_3 (nand_3_out, in_3, clock_1_out);
  nand nand_4 (nand_4_out, clock_1_out, not_2_out);
  nand nand_5 (out_4, nand_1_out, out_5);
  nand nand_6 (out_5, out_4, nand_2_out);
  nand nand_7 (out_6, nand_3_out, out_7);
  nand nand_8 (out_7, out_6, nand_4_out);

  assign in_2 = in_1;

  // Notes on the sheet:
  //   D Latch
  //   Flip Flop
endmodule
