// Logisim project 6_cameronpierce.circ as structural Verilog: 1 circuit, main circuit main
module main (
  input  [2:0] in_1,
  input  [2:0] in_2,
  input  in_3,
  input  in_4,
  output [2:0] out_5
);

  wire and_1_out, and_2_out, and_3_out, and_4_out, and_5_out, d_ff_3_q, decoder_1_out0, decoder_1_out1,
       decoder_1_out2, decoder_1_out3, decoder_1_out4;
  wire [2:0] d_ff_11_q, d_ff_12_q, d_ff_13_q, d_ff_14_q, d_ff_15_q;

  Decoder #(.select(3)) decoder_1 (
    .out0(decoder_1_out0), .out1(decoder_1_out1), .out2(decoder_1_out2), .out3(decoder_1_out3),
    .out4(decoder_1_out4), .sel(in_2));  // open: out5, out6, out7, en
  buf and_1 (and_1_out, decoder_1_out0);  // AND_Gate
  buf and_2 (and_2_out, decoder_1_out1);  // AND_Gate
  buf and_3 (and_3_out, decoder_1_out2);  // AND_Gate
  buf and_4 (and_4_out, decoder_1_out3);  // AND_Gate
  and and_5 (and_5_out, decoder_1_out4, in_3);
  D_Flip_Flop d_ff_1 (.D(in_1[2]), .clk(and_1_out), .Q(d_ff_11_q[2]), .reset(in_4));  // open: Qn, preset
  D_Flip_Flop d_ff_2 (.D(in_1[2]), .clk(and_2_out), .Q(d_ff_12_q[2]), .reset(in_4));  // open: Qn, preset
  D_Flip_Flop d_ff_3 (.D(in_1[2]), .clk(and_3_out), .Q(d_ff_3_q), .reset(in_4));  // open: Qn, preset
  D_Flip_Flop d_ff_4 (.D(in_1[2]), .clk(and_4_out), .Q(d_ff_14_q[2]));  // open: Qn, preset, reset
  D_Flip_Flop d_ff_5 (.D(in_1[2]), .clk(and_5_out), .Q(d_ff_15_q[2]), .reset(in_4));  // open: Qn, preset
  D_Flip_Flop d_ff_6 (.D(in_1[1]), .clk(and_1_out), .Q(d_ff_11_q[1]), .reset(in_4));  // open: Qn, preset
  D_Flip_Flop d_ff_7 (.D(in_1[1]), .clk(and_2_out), .Q(d_ff_12_q[1]), .reset(in_4));  // open: Qn, preset
  D_Flip_Flop d_ff_8 (.D(in_1[1]), .clk(and_3_out), .Q(d_ff_13_q[1]), .reset(in_4));  // open: Qn, preset
  D_Flip_Flop d_ff_9 (.D(in_1[1]), .clk(and_4_out), .Q(d_ff_14_q[1]));  // open: Qn, preset, reset
  D_Flip_Flop d_ff_10 (.D(in_1[1]), .clk(and_5_out), .Q(d_ff_15_q[1]), .reset(in_4));  // open: Qn, preset
  D_Flip_Flop d_ff_11 (.D(in_1[0]), .clk(and_1_out), .Q(d_ff_11_q[0]), .reset(in_4));  // open: Qn, preset
  D_Flip_Flop d_ff_12 (.D(in_1[0]), .clk(and_2_out), .Q(d_ff_12_q[0]), .reset(in_4));  // open: Qn, preset
  D_Flip_Flop d_ff_13 (.D(in_1[0]), .clk(and_3_out), .Q(d_ff_13_q[0]), .reset(in_4));  // open: Qn, preset
  D_Flip_Flop d_ff_14 (.D(in_1[0]), .clk(and_4_out), .Q(d_ff_14_q[0]));  // open: Qn, preset, reset
  D_Flip_Flop d_ff_15 (.D(in_1[0]), .clk(and_5_out), .Q(d_ff_15_q[0]), .reset(in_4));  // open: Qn, preset
  Multiplexer #(.select(3), .width(3)) multiplexer_1 (
    .in0(d_ff_11_q), .in1(d_ff_11_q), .in2(d_ff_11_q), .in3(d_ff_12_q), .in4(d_ff_13_q), .in5(d_ff_14_q),
    .in6(d_ff_15_q), .in7(d_ff_15_q), .out(out_5), .sel(in_2));
endmodule
